// Logisim project Hmm.circ as structural Verilog: 3 circuits, main circuit main
module main (
);

  CPU cpu_1 ();  // open: Reset, ClockPin
  // RGB_Video #(.cursor("No Cursor")) rgb_video_1: pin names not known
endmodule

module CPU (
  input  Reset,
  input  ClockPin
);

  wire A_in, Address_in, Address_out, Alternator_q, Alternator_qn, and_1_out, and_2_out, and_4_out,
       and_5_out, and_6_out, and_7_out, and_8_out, AO_in, AO_out, B_in, Clk, clock_1_out, ClockBtn_out,
       d_ff_1_q, d_ff_2_q, decoder_1_out0, decoder_1_out1, decoder_1_out2, decoder_1_out3, decoder_2_out10,
       decoder_2_out11, decoder_2_out12, decoder_2_out13, decoder_2_out15, decoder_3_out12, decoder_3_out13,
       decoder_3_out14, decoder_3_out15, decoder_4_out0, decoder_4_out1, decoder_4_out2, decoder_4_out3,
       decoder_4_out4, decoder_4_out5, decoder_4_out6, decoder_4_out7, decoder_4_out8, decoder_4_out9,
       decoder_4_out10, decoder_4_out11, decoder_4_out12, decoder_4_out13, decoder_4_out14, decoder_4_out15,
       demultiplexer_1_out0, demultiplexer_1_out1, Halt, JumpFlag, MAR_in, math_1_log_cmp, math_1_log_val,
       Math_Flags_In, MDR_out, MWR_in, nor_1_out, not_1_out, not_2_out, not_3_out, not_4_out, or_2_out,
       or_3_out, or_4_out, or_5_out, or_6_out, or_7_out, or_8_out, PC_in, PC_out, R0_in, R0_out, R1_in,
       R1_out, R2_in, R2_out, R3_in, R3_out, Reset_t, RstBtn_out, Value_in, Value_out, Y_out;
  wire [1:0] MainCounter_q;
  wire [3:0] Math_Flags, MathFlags_q;
  wire [7:4] MicrocodeROM_data;
  wire [11:0] MicroPC_q;
  wire [15:0] A_q, Address_q, AOffset_q, B_q, controlled_buffer_1_out, MainRAM_dout, MAR_q, math_1_y, PC_q,
       R0_q, R1_q, R2_q, R3_q, Value_q;

  Button RstBtn (.out(RstBtn_out));
  or or_1 (Reset_t, RstBtn_out, Reset);
  Clock clock_1 (.out(clock_1_out));
  or or_2 (or_2_out, clock_1_out, ClockBtn_out, ClockPin);
  Button ClockBtn (.out(ClockBtn_out));
  not not_1 (not_1_out, Halt);
  T_Flip_Flop Alternator (
    .T(1'b1), .clk(nor_1_out), .Q(Alternator_q), .Qn(Alternator_qn), .reset(Reset_t));  // open: preset
  nor nor_1 (nor_1_out, Reset_t, and_1_out);
  and and_1 (and_1_out, or_2_out, not_1_out);
  Demultiplexer demultiplexer_1 (
    .out0(demultiplexer_1_out0), .out1(demultiplexer_1_out1), .in(and_2_out), .sel(decoder_1_out3));
  and and_2 (and_2_out, Alternator_q, and_1_out);
  and and_3 (Clk, Alternator_qn, and_1_out);
  or or_3 (or_3_out, Reset_t, d_ff_2_q);
  and and_4 (and_4_out, decoder_1_out2, Clk);
  and and_5 (and_5_out, demultiplexer_1_out1, d_ff_1_q);
  or or_4 (or_4_out, Reset_t, decoder_1_out2);
  D_Flip_Flop d_ff_1 (.D(Clk), .clk(Clk), .Q(d_ff_1_q), .reset(or_4_out));  // open: Qn, preset
  Counter #(.max('h3), .width(2)) MainCounter (
    .clr(or_3_out), .load(1'b0), .up(1'b1), .count(1'b1), .clk(demultiplexer_1_out0), .Q(MainCounter_q));  // open: D, carry
  Counter #(.max('hfff), .width(12)) MicroPC (
    .clr(decoder_1_out0), .load(decoder_1_out2), .up(1'b1), .count(1'b1), .clk(or_5_out),
    .D({controlled_buffer_1_out[7:0], 4'b0000}), .Q(MicroPC_q));  // open: carry
  or or_5 (or_5_out, and_4_out, and_5_out);
  Decoder #(.enable("false"), .select(2)) decoder_1 (
    .out0(decoder_1_out0), .out1(decoder_1_out1), .out2(decoder_1_out2), .out3(decoder_1_out3),
    .sel(MainCounter_q));
  ROM #(.addrWidth(12)) MicrocodeROM (.addr(MicroPC_q), .data({MicrocodeROM_data, Math_Flags}));
  not not_2 (not_2_out, decoder_2_out15);
  not not_3 (not_3_out, Math_Flags_In);
  and and_6 (and_6_out, decoder_2_out15, decoder_1_out3);
  and and_7 (and_7_out, not_2_out, not_3_out, decoder_1_out3);
  Counter #(.max('hffff), .width(16)) PC (
    .clr(Reset_t), .load(1'b0), .up(1'b1), .count(decoder_1_out0), .clk(Clk), .Q(PC_q));  // open: D, carry
  Decoder #(.select(4)) decoder_2 (
    .out0(R0_out), .out1(R1_out), .out2(R2_out), .out3(R3_out), .out4(PC_out), .out5(Value_out),
    .out6(Address_out), .out7(MDR_out), .out8(Y_out), .out9(AO_out), .out10(decoder_2_out10),
    .out11(decoder_2_out11), .out12(decoder_2_out12), .out13(decoder_2_out13), .out14(Math_Flags_In),
    .out15(decoder_2_out15), .sel(MicrocodeROM_data), .en(decoder_1_out3));
  Decoder #(.select(4)) decoder_3 (
    .out0(R0_in), .out1(R1_in), .out2(R2_in), .out3(R3_in), .out4(PC_in), .out5(Value_in), .out6(Address_in),
    .out7(MWR_in), .out8(MAR_in), .out9(A_in), .out10(B_in), .out11(AO_in), .out12(decoder_3_out12),
    .out13(decoder_3_out13), .out14(decoder_3_out14), .out15(decoder_3_out15), .sel(Math_Flags),
    .en(and_7_out));
  D_Flip_Flop d_ff_2 (.D(decoder_4_out15), .clk(Clk), .Q(d_ff_2_q), .reset(Reset_t));  // open: Qn, preset
  Decoder #(.select(4)) decoder_4 (
    .out0(decoder_4_out0), .out1(decoder_4_out1), .out2(decoder_4_out2), .out3(decoder_4_out3),
    .out4(decoder_4_out4), .out5(decoder_4_out5), .out6(decoder_4_out6), .out7(decoder_4_out7),
    .out8(decoder_4_out8), .out9(decoder_4_out9), .out10(decoder_4_out10), .out11(decoder_4_out11),
    .out12(decoder_4_out12), .out13(decoder_4_out13), .out14(decoder_4_out14), .out15(decoder_4_out15),
    .sel(Math_Flags), .en(and_6_out));
  D_Flip_Flop d_ff_3 (.D(decoder_4_out14), .clk(Clk), .Q(Halt), .reset(Reset_t));  // open: Qn, preset
  assign controlled_buffer_1_out = or_6_out ? PC_q : 16'bz;  // Controlled_Buffer controlled_buffer_1
  or or_6 (or_6_out, PC_out, decoder_1_out1);
  Register #(.width(16)) AOffset (.D(controlled_buffer_1_out), .en(AO_in), .clk(Clk), .Q(AOffset_q), .clr(Reset_t));
  assign controlled_buffer_1_out = AO_out ? AOffset_q : 16'bz;  // Controlled_Buffer controlled_buffer_2
  or or_7 (or_7_out, MAR_in, decoder_1_out1);
  Register #(.width(16)) MAR (.D(controlled_buffer_1_out), .en(or_7_out), .clk(Clk), .Q(MAR_q), .clr(Reset_t));
  not not_4 (not_4_out, Clk);
  RAM #(.addrWidth(16), .dataWidth(16)) MainRAM (
    .addr(MAR_q), .we(MWR_in), .oe(1'b1), .clk(not_4_out), .din(controlled_buffer_1_out), .dout(MainRAM_dout));
  Register #(.width(16)) R0 (.D(controlled_buffer_1_out), .en(R0_in), .clk(Clk), .Q(R0_q), .clr(Reset_t));
  Register #(.width(16)) R1 (.D(controlled_buffer_1_out), .en(R1_in), .clk(Clk), .Q(R1_q), .clr(Reset_t));
  Register #(.width(16)) R2 (.D(controlled_buffer_1_out), .en(R2_in), .clk(Clk), .Q(R2_q), .clr(Reset_t));
  Register #(.width(16)) R3 (.D(controlled_buffer_1_out), .en(R3_in), .clk(Clk), .Q(R3_q), .clr(Reset_t));
  Register #(.width(16)) Value (.D(controlled_buffer_1_out), .en(Value_in), .clk(Clk), .Q(Value_q), .clr(Reset_t));
  Register #(.width(16)) Address (
    .D(controlled_buffer_1_out), .en(Address_in), .clk(Clk), .Q(Address_q), .clr(Reset_t));
  assign controlled_buffer_1_out = or_8_out ? MainRAM_dout : 16'bz;  // Controlled_Buffer controlled_buffer_3
  or or_8 (or_8_out, decoder_1_out2, MDR_out);
  assign controlled_buffer_1_out = R0_out ? R0_q : 16'bz;  // Controlled_Buffer controlled_buffer_4
  assign controlled_buffer_1_out = R1_out ? R1_q : 16'bz;  // Controlled_Buffer controlled_buffer_5
  assign controlled_buffer_1_out = R2_out ? R2_q : 16'bz;  // Controlled_Buffer controlled_buffer_6
  assign controlled_buffer_1_out = R3_out ? R3_q : 16'bz;  // Controlled_Buffer controlled_buffer_7
  assign controlled_buffer_1_out = Value_out ? Value_q : 16'bz;  // Controlled_Buffer controlled_buffer_8
  assign controlled_buffer_1_out = Address_out ? Address_q : 16'bz;  // Controlled_Buffer controlled_buffer_9
  Register #(.width(16)) A (.D(controlled_buffer_1_out), .en(A_in), .clk(Clk), .Q(A_q), .clr(Reset_t));
  Register #(.width(16)) B (.D(controlled_buffer_1_out), .en(B_in), .clk(Clk), .Q(B_q), .clr(Reset_t));
  Register #(.width(4)) MathFlags (.D(Math_Flags), .en(Math_Flags_In), .clk(Clk), .Q(MathFlags_q), .clr(Reset_t));
  Math math_1 (.A(A_q), .B(B_q), .Flags(MathFlags_q), .Y(math_1_y), .Log_Cmp(math_1_log_cmp), .Log_Val(math_1_log_val));
  D_Flip_Flop u_JumpFlag (.D(math_1_log_val), .clk(and_8_out), .Q(JumpFlag), .reset(Reset_t));  // open: Qn, preset
  and and_8 (and_8_out, math_1_log_cmp, Clk);
  assign controlled_buffer_1_out = Y_out ? math_1_y : 16'bz;  // Controlled_Buffer controlled_buffer_10

  // Notes on the sheet:
  //   contents of MicrocodeROM (hex, n*v repeats v):
  //   16*ff f3 48 78 75 f3 48 78 57 8*ff f3 48 76 13*ff f3 48 78 76 12*ff 6 15*ff 16 15*ff 26 15*ff 36
  //   15*ff f3 48 70 13*ff f3 48 71 13*ff f3 48 72 13*ff f3 48 73 13*ff f3 48 78 70 12*ff f3 48 78 71
  //   12*ff f3 48 78 72 12*ff f3 48 78 73 12*ff 68 70 14*ff 68 71 14*ff 68 72 14*ff 68 73 14*ff f3 48 78 7
  //   12*ff f3 48 78 17 12*ff f3 48 78 27 12*ff f3 48 78 37 12*ff f3 48 75 8 57 11*ff f3 48 75 18 57 11*ff
  //   f3 48 75 28 57 11*ff f3 48 75 38 57 11*ff f3 48 75 f3 48 78 57 9*ff f3 48 75 68 57 11*ff 68 75 f3 48
  //   78 57 26*ff 68 7 14*ff 68 17 14*ff 68 27 14*ff 68 37 398*ff 9 f3 48 7a e0 80 10*ff 19 f3 48 7a e0 81
  //   10*ff 29 f3 48 7a e0 82 10*ff 39 f3 48 7a e0 83 138*ff 9 f3 48 7a e1 80 10*ff 19 f3 48 7a e1 81
  //   10*ff 29 f3 48 7a e1 82 10*ff 39 f3 48 7a e1 83 1290*ff 0 15*ff 10 15*ff 20 15*ff 30 15*ff 0 15*ff 1
  //   15*ff 2 15*ff 3 847*ff f3 48 74 13*ff 64 143*ff fe 15*ff fe 15*ff c 15*ff 1c 15*ff 2c 15*ff 3c 15*ff
  //   f3 48 7c 13*ff f3 48 78 7c 12*ff f3 48 78 7d 12*ff f3 48 7d 13*ff d 15*ff 1d 15*ff 2d 15*ff 3d 15*ff
  //   b 15*ff 1b 15*ff 2b 15*ff 3b 15*ff f3 48 7b 13*ff f3 48 78 7b 12*ff f5 15*ff f6 15*ff f2 15*ff f1
  //   15*ff 90 15*ff
  //   PC++, MPC=0
  //   PC -> MAR
  //   MDR -> InstR
  //   Microcode
endmodule

module Math (
  input  [15:0] A,
  input  [15:0] B,
  input  [3:0] Flags,
  output [15:0] Y,
  output Log_Cmp,
  output Log_Val
);

  wire adder_1_cout, and_1_out, and_3_out, and_4_out, and_5_out, and_6_out, and_7_out, and_8_out, and_9_out,
       and_10_out, and_11_out, decoder_1_out0, decoder_1_out1, decoder_1_out2, decoder_1_out3, not_1_out,
       not_4_out, not_5_out, not_6_out, not_7_out, not_8_out, not_9_out, not_10_out, not_11_out, or_1_out,
       or_2_out, or_4_out;
  wire [15:0] adder_1_out, and_2_out, multiplexer_1_out, multiplexer_2_out, multiplexer_3_out, not_2_out,
       not_3_out, or_3_out, shifter_1_out, shifter_2_out, xor_1_out;

  and and_1 (and_1_out, Flags[1], not_1_out);
  not not_1 (not_1_out, Flags[3]);
  Multiplexer #(.width(16)) multiplexer_1 (.in0(B), .in1(16'h1), .out(multiplexer_1_out), .sel(and_1_out));
  assign not_2_out = ~multiplexer_1_out;  // NOT_Gate not_2, 16 bits wide
  Multiplexer #(.width(16)) multiplexer_2 (
    .in0(multiplexer_1_out), .in1(not_2_out), .out(multiplexer_2_out), .sel(or_1_out));
  or or_1 (or_1_out, Flags[0], Flags[3]);
  or or_2 (or_2_out, Flags[0], Flags[1]);
  Multiplexer #(.width(16)) multiplexer_3 (.in0(A), .in1(xor_1_out), .out(multiplexer_3_out), .sel(or_2_out));
  assign not_3_out = ~A;  // NOT_Gate not_3, 16 bits wide
  assign xor_1_out = A ^ B;  // XOR_Gate xor_1, 16 bits wide
  assign or_3_out = A | B;  // OR_Gate or_3, 16 bits wide
  assign and_2_out = A & B;  // AND_Gate and_2, 16 bits wide
  Shifter #(.shift("lr"), .width(16)) shifter_1 (.in(A), .\dist (multiplexer_1_out[3:0]), .out(shifter_1_out));
  assign Y = and_3_out ? shifter_2_out : 16'bz;  // Controlled_Buffer controlled_buffer_1
  Shifter #(.width(16)) shifter_2 (.in(A), .\dist (multiplexer_1_out[3:0]), .out(shifter_2_out));
  and and_3 (and_3_out, Flags[2], not_4_out, not_5_out);
  assign Y = and_4_out ? adder_1_out : 16'bz;  // Controlled_Buffer controlled_buffer_2
  Adder #(.width(16)) adder_1 (.a(A), .b(multiplexer_2_out), .out(adder_1_out), .cin(or_1_out), .cout(adder_1_cout));
  and and_4 (and_4_out, not_6_out, not_7_out);
  not not_4 (not_4_out, Flags[3]);
  not not_5 (not_5_out, Flags[0]);
  not not_6 (not_6_out, Flags[2]);
  not not_7 (not_7_out, Flags[3]);
  or or_4 (or_4_out, multiplexer_3_out[0], multiplexer_3_out[1], multiplexer_3_out[2], multiplexer_3_out[3], multiplexer_3_out[4], multiplexer_3_out[5], multiplexer_3_out[6], multiplexer_3_out[7], multiplexer_3_out[8], multiplexer_3_out[9], multiplexer_3_out[10], multiplexer_3_out[11], multiplexer_3_out[12], multiplexer_3_out[13], multiplexer_3_out[14], multiplexer_3_out[15]);
  assign Y = and_5_out ? not_3_out : 16'bz;  // Controlled_Buffer controlled_buffer_3
  and and_5 (and_5_out, and_10_out, decoder_1_out3);
  assign Y = and_6_out ? xor_1_out : 16'bz;  // Controlled_Buffer controlled_buffer_4
  and and_6 (and_6_out, and_10_out, decoder_1_out2);
  assign Y = and_7_out ? or_3_out : 16'bz;  // Controlled_Buffer controlled_buffer_5
  and and_7 (and_7_out, and_10_out, decoder_1_out1);
  assign Y = and_8_out ? and_2_out : 16'bz;  // Controlled_Buffer controlled_buffer_6
  and and_8 (and_8_out, and_10_out, decoder_1_out0);
  assign Y = and_9_out ? shifter_1_out : 16'bz;  // Controlled_Buffer controlled_buffer_7
  and and_9 (and_9_out, Flags[2], not_4_out, not_8_out);
  and and_10 (and_10_out, Flags[3], not_11_out);
  not not_8 (not_8_out, not_5_out);
  not not_9 (not_9_out, adder_1_cout);
  and and_11 (and_11_out, adder_1_cout, or_4_out);
  not not_10 (not_10_out, or_4_out);
  Decoder #(.enable("false"), .select(2)) decoder_1 (
    .out0(decoder_1_out0), .out1(decoder_1_out1), .out2(decoder_1_out2), .out3(decoder_1_out3),
    .sel(Flags[1:0]));
  not not_11 (not_11_out, Flags[2]);
  and and_12 (Log_Cmp, Flags[2], Flags[3]);
  Multiplexer #(.select(2)) multiplexer_4 (
    .in0(not_10_out), .in1(not_10_out), .in2(not_9_out), .in3(and_11_out), .out(Log_Val), .sel(Flags[1:0]));

  // Notes on the sheet:
  //   A >= B
endmodule
