// Logisim project HmmNoHard.circ as structural Verilog: 5 circuits, main circuit main
module main (
);

  wire button_1_out, button_2_out, button_3_out, cpu_1_halt, cpu_1_ram_clock, cpu_1_ram_we, cpu_1_tty_clock,
       cpu_1_tty_write;
  wire [6:0] cpu_1_tty_ascii;
  wire [15:0] cpu_1_ram_addr, cpu_1_ram_data, ram_1_dout;

  Button button_1 (.out(button_1_out));
  Button button_2 (.out(button_2_out));
  RAM #(.addrWidth(16), .dataWidth(16)) ram_1 (
    .addr(cpu_1_ram_addr), .we(cpu_1_ram_we), .oe(1'b1), .clk(cpu_1_ram_clock), .din(cpu_1_ram_data),
    .dout(ram_1_dout));
  CPU cpu_1 (
    .Reset(button_1_out), .ClockPin(button_2_out), .RAM_out(ram_1_dout), .RAM_Addr(cpu_1_ram_addr),
    .RAM_WE(cpu_1_ram_we), .RAM_Clock(cpu_1_ram_clock), .RAM_Data(cpu_1_ram_data),
    .TTY_ASCII(cpu_1_tty_ascii), .TTY_Clock(cpu_1_tty_clock), .TTY_Write(cpu_1_tty_write), .Halt(cpu_1_halt));
  TTY tty_1 (.data(cpu_1_tty_ascii), .clk(cpu_1_tty_clock), .we(cpu_1_tty_write), .clr(button_3_out));
  Button button_3 (.out(button_3_out));
  LED led_1 (.in(cpu_1_halt));
  // RGB_Video #(.cursor("No Cursor")) rgb_video_1: pin names not known
endmodule

module CPU (
  input  Reset,
  input  ClockPin,
  input  [15:0] RAM_out,
  output [15:0] RAM_Addr,
  output RAM_WE,
  output RAM_Clock,
  output [15:0] RAM_Data,
  output [6:0] TTY_ASCII,
  output TTY_Clock,
  output TTY_Write,
  output Halt
);

  wire A_in, Address_in, Address_out, Alternator_q, Alternator_qn, and_1_out, and_3_out, and_4_out,
       and_5_out, and_6_out, and_7_out, and_8_out, and_9_out, and_10_out, AO_in, AO_out, B_in, button_1_out,
       Clk, clock_1_out, ClockBtn_out, Cond_out, d_ff_1_q, DBG_in, DBGC_in, decoder_1_out12, decoder_1_out13,
       decoder_1_out15, decoder_2_out15, decoder_3_out0, decoder_3_out1, decoder_3_out2, decoder_3_out3,
       decoder_3_out4, decoder_3_out5, decoder_3_out6, decoder_3_out7, decoder_3_out10, decoder_3_out11,
       decoder_3_out12, decoder_3_out13, decoder_3_out14, decoder_3_out15, demultiplexer_2_out1,
       demultiplexer_3_out1, JumpFlag, MAR_in, math_1_log_cmp, math_1_log_val, Math_Flags_In, MDR_out,
       MPC_in, MPC_Reset, MWR_in, nor_1_out, not_1_out, not_2_out, not_3_out, not_4_out, not_5_out,
       not_6_out, or_2_out, or_3_out, or_4_out, or_5_out, or_6_out, or_7_out, or_8_out, or_9_out, PC_in,
       PC_out, R0_in, R0_out, R1_in, R1_out, R2_in, R2_out, R3_in, R3_out, Reset_t, RstBtn_out, SP_out,
       Value_in, Value_out, x00_B, xff_B, Y_out;
  wire [3:0] Math_Flags, MicrocodeROM_data;
  wire [7:0] controlled_buffer_1_out, controlled_buffer_1_out_2;
  wire [11:0] MicroPC_q;
  wire [15:0] A_q, Address_q, AOffset_q, B_q, demultiplexer_1_out1, demultiplexer_4_out1, MainRAM_dout,
       MAR_q, math_1_y, multiplexer_1_out, PC_q, R0_q, R1_q, R2_q, R3_q, Value_q, Y_q;

  Button RstBtn (.out(RstBtn_out));
  or or_1 (Reset_t, RstBtn_out, Reset);
  Clock clock_1 (.out(clock_1_out));
  or or_2 (or_2_out, clock_1_out, ClockBtn_out, ClockPin);
  Button ClockBtn (.out(ClockBtn_out));
  not not_1 (not_1_out, Halt);
  T_Flip_Flop Alternator (
    .T(1'b1), .clk(nor_1_out), .Q(Alternator_q), .Qn(Alternator_qn), .reset(Reset_t));  // open: preset
  nor nor_1 (nor_1_out, Reset_t, and_1_out);
  and and_1 (and_1_out, or_2_out, not_1_out);
  and and_2 (Clk, Alternator_q, and_1_out);
  and and_3 (and_3_out, Alternator_qn, and_1_out);
  D_Flip_Flop d_ff_1 (.D(Clk), .clk(Clk), .Q(d_ff_1_q), .reset(or_3_out));  // open: Qn, preset
  or or_3 (or_3_out, Reset_t, MPC_in);
  or or_4 (or_4_out, MPC_in, Reset_t);
  and and_4 (and_4_out, and_3_out, d_ff_1_q);
  or or_5 (or_5_out, and_4_out, Clk);
  or or_6 (or_6_out, MPC_Reset, Reset_t);
  Counter #(.max('hfff), .width(12)) MicroPC (
    .clr(or_6_out), .load(or_4_out), .up(1'b1), .count(and_4_out), .clk(or_5_out),
    .D({controlled_buffer_1_out, 4'b0000}), .Q(MicroPC_q));  // open: carry
  assign {controlled_buffer_1_out_2, controlled_buffer_1_out} = SP_out ? 16'hf000 : 16'bz;  // Controlled_Buffer controlled_buffer_1
  Register #(.width(16)) PC (
    .D({controlled_buffer_1_out_2, controlled_buffer_1_out}), .en(PC_in), .clk(Clk), .Q(PC_q), .clr(Reset_t));
  not not_2 (not_2_out, decoder_1_out15);
  not not_3 (not_3_out, Math_Flags_In);
  assign {controlled_buffer_1_out_2, controlled_buffer_1_out} = x00_B ? {16{1'b0}} : 16'bz;  // Controlled_Buffer controlled_buffer_2
  assign {controlled_buffer_1_out_2, controlled_buffer_1_out} = PC_out ? PC_q : 16'bz;  // Controlled_Buffer controlled_buffer_3
  Decoder #(.enable("false"), .select(4)) decoder_1 (
    .out0(R0_out), .out1(R1_out), .out2(R2_out), .out3(R3_out), .out4(PC_out), .out5(Value_out),
    .out6(Address_out), .out7(MDR_out), .out8(Y_out), .out9(AO_out), .out10(SP_out), .out11(Cond_out),
    .out12(decoder_1_out12), .out13(decoder_1_out13), .out14(Math_Flags_In), .out15(decoder_1_out15),
    .sel(MicrocodeROM_data));
  and and_5 (and_5_out, not_2_out, not_3_out);
  Decoder #(.select(4)) decoder_2 (
    .out0(R0_in), .out1(R1_in), .out2(R2_in), .out3(R3_in), .out4(PC_in), .out5(Value_in), .out6(Address_in),
    .out7(MWR_in), .out8(MAR_in), .out9(A_in), .out10(B_in), .out11(AO_in), .out12(DBG_in), .out13(DBGC_in),
    .out14(MPC_in), .out15(decoder_2_out15), .sel(Math_Flags), .en(and_5_out));
  Decoder #(.select(4)) decoder_3 (
    .out0(decoder_3_out0), .out1(decoder_3_out1), .out2(decoder_3_out2), .out3(decoder_3_out3),
    .out4(decoder_3_out4), .out5(decoder_3_out5), .out6(decoder_3_out6), .out7(decoder_3_out7), .out8(x00_B),
    .out9(xff_B), .out10(decoder_3_out10), .out11(decoder_3_out11), .out12(decoder_3_out12),
    .out13(decoder_3_out13), .out14(decoder_3_out14), .out15(decoder_3_out15), .sel(Math_Flags),
    .en(decoder_1_out15));
  Register #(.width(16)) R0 (
    .D({controlled_buffer_1_out_2, controlled_buffer_1_out}), .en(R0_in), .clk(Clk), .Q(R0_q), .clr(Reset_t));
  ROM #(.addrWidth(12)) MicrocodeROM (.addr(MicroPC_q), .data({MicrocodeROM_data, Math_Flags}));
  not not_4 (not_4_out, JumpFlag);
  and and_6 (and_6_out, JumpFlag, decoder_3_out13);
  or or_7 (or_7_out, decoder_3_out15, and_6_out, and_7_out);
  D_Flip_Flop #(.trigger("falling")) d_ff_2 (.D(or_7_out), .clk(and_3_out), .Q(MPC_Reset));  // open: Qn, preset, reset
  assign {controlled_buffer_1_out_2, controlled_buffer_1_out} = xff_B ? {16{1'b1}} : 16'bz;  // Controlled_Buffer controlled_buffer_4
  assign {controlled_buffer_1_out_2, controlled_buffer_1_out} = R0_out ? R0_q : 16'bz;  // Controlled_Buffer controlled_buffer_5
  and and_7 (and_7_out, not_4_out, decoder_3_out12);
  Register #(.width(16)) R1 (
    .D({controlled_buffer_1_out_2, controlled_buffer_1_out}), .en(R1_in), .clk(Clk), .Q(R1_q), .clr(Reset_t));
  D_Flip_Flop d_ff_3 (.D(decoder_3_out14), .clk(Clk), .Q(Halt), .reset(Reset_t));  // open: Qn, preset
  assign {controlled_buffer_1_out_2, controlled_buffer_1_out} = R1_out ? R1_q : 16'bz;  // Controlled_Buffer controlled_buffer_6
  Register #(.width(16)) R2 (
    .D({controlled_buffer_1_out_2, controlled_buffer_1_out}), .en(R2_in), .clk(Clk), .Q(R2_q), .clr(Reset_t));
  LED led_1 (.in(Halt));
  assign {controlled_buffer_1_out_2, controlled_buffer_1_out} = R2_out ? R2_q : 16'bz;  // Controlled_Buffer controlled_buffer_7
  Register #(.width(16)) R3 (
    .D({controlled_buffer_1_out_2, controlled_buffer_1_out}), .en(R3_in), .clk(Clk), .Q(R3_q), .clr(Reset_t));
  Register #(.width(16)) A (
    .D({controlled_buffer_1_out_2, controlled_buffer_1_out}), .en(A_in), .clk(Clk), .Q(A_q), .clr(Reset_t));
  Register #(.width(16)) B (
    .D({controlled_buffer_1_out_2, controlled_buffer_1_out}), .en(or_8_out), .clk(Clk), .Q(B_q), .clr(Reset_t));
  or or_8 (or_8_out, B_in, x00_B, xff_B);
  assign {controlled_buffer_1_out_2, controlled_buffer_1_out} = R3_out ? R3_q : 16'bz;  // Controlled_Buffer controlled_buffer_8
  Register #(.width(16)) Value (
    .D({controlled_buffer_1_out_2, controlled_buffer_1_out}), .en(Value_in), .clk(Clk), .Q(Value_q),
    .clr(Reset_t));
  and and_8 (and_8_out, math_1_log_cmp, Math_Flags_In);
  DBG_out dbg_out_1 (
    .Data_in({controlled_buffer_1_out_2, controlled_buffer_1_out}), .DBG_in(DBG_in), .DBGC_in(DBGC_in),
    .Clk(Clk), .Reset(Reset_t), .TTY_ASCII(TTY_ASCII), .TTY_Clock(TTY_Clock), .TTY_Write(TTY_Write));
  assign {controlled_buffer_1_out_2, controlled_buffer_1_out} = Value_out ? Value_q : 16'bz;  // Controlled_Buffer controlled_buffer_9
  Math math_1 (.A(A_q), .B(B_q), .Flags(Math_Flags), .Y(math_1_y), .Log_Cmp(math_1_log_cmp), .Log_Val(math_1_log_val));
  Register #(.width(16)) Address (
    .D({controlled_buffer_1_out_2, controlled_buffer_1_out}), .en(Address_in), .clk(Clk), .Q(Address_q),
    .clr(Reset_t));
  not not_5 (not_5_out, math_1_log_cmp);
  and and_9 (and_9_out, not_5_out, Math_Flags_In);
  D_Flip_Flop u_JumpFlag (.D(math_1_log_val), .clk(and_10_out), .Q(JumpFlag), .reset(Reset_t));  // open: Qn, preset
  and and_10 (and_10_out, and_8_out, Clk);
  TTY tty_1 (.data(TTY_ASCII), .clk(TTY_Clock), .we(TTY_Write), .clr(or_9_out));
  assign {controlled_buffer_1_out_2, controlled_buffer_1_out} = Address_out ? Address_q : 16'bz;  // Controlled_Buffer controlled_buffer_10
  Register #(.width(16)) Y (.D(math_1_y), .en(and_9_out), .clk(Clk), .Q(Y_q), .clr(Reset_t));
  or or_9 (or_9_out, Reset_t, button_1_out);
  Button button_1 (.out(button_1_out));
  Register #(.width(16)) AOffset (
    .D({controlled_buffer_1_out_2, controlled_buffer_1_out}), .en(AO_in), .clk(Clk), .Q(AOffset_q),
    .clr(Reset_t));
  assign {controlled_buffer_1_out_2, controlled_buffer_1_out} = AO_out ? AOffset_q : 16'bz;  // Controlled_Buffer controlled_buffer_11
  assign {controlled_buffer_1_out_2, controlled_buffer_1_out} = Y_out ? Y_q : 16'bz;  // Controlled_Buffer controlled_buffer_12
  assign {controlled_buffer_1_out_2, controlled_buffer_1_out} = Cond_out ? {16{JumpFlag}} : 16'bz;  // Controlled_Buffer controlled_buffer_13
  Register #(.width(16)) MAR (
    .D({controlled_buffer_1_out_2, controlled_buffer_1_out}), .en(MAR_in), .clk(Clk), .Q(MAR_q), .clr(Reset_t));
  Demultiplexer #(.width(16)) demultiplexer_1 (.out0(RAM_Addr), .out1(demultiplexer_1_out1), .in(MAR_q), .sel(1'b1));
  Demultiplexer demultiplexer_2 (.out0(RAM_WE), .out1(demultiplexer_2_out1), .in(MWR_in), .sel(1'b1));
  Demultiplexer demultiplexer_3 (.out0(RAM_Clock), .out1(demultiplexer_3_out1), .in(not_6_out), .sel(1'b1));
  Demultiplexer #(.width(16)) demultiplexer_4 (
    .out0(RAM_Data), .out1(demultiplexer_4_out1), .in({controlled_buffer_1_out_2, controlled_buffer_1_out}),
    .sel(1'b1));
  not not_6 (not_6_out, Clk);
  RAM #(.addrWidth(16), .dataWidth(16)) MainRAM (
    .addr(demultiplexer_1_out1), .we(demultiplexer_2_out1), .oe(1'b1), .clk(demultiplexer_3_out1),
    .din(demultiplexer_4_out1), .dout(MainRAM_dout));
  assign {controlled_buffer_1_out_2, controlled_buffer_1_out} = MDR_out ? multiplexer_1_out : 16'bz;  // Controlled_Buffer controlled_buffer_14
  Multiplexer #(.width(16)) multiplexer_1 (.in0(RAM_out), .in1(MainRAM_dout), .out(multiplexer_1_out), .sel(1'b1));

  // Notes on the sheet:
  //   contents of MicrocodeROM (hex, n*v repeats v):
  //   48 49 e2 84 7e 11*ff 48 49 e2 84 78 75 48 49 e2 84 78 57 4*ff 48 49 e2 84 76 11*ff 48 49 e2 84 78 76
  //   10*ff 6 15*ff 16 15*ff 26 15*ff 36 15*ff 48 49 e2 84 70 11*ff 48 49 e2 84 71 11*ff 48 49 e2 84 72
  //   11*ff 48 49 e2 84 73 11*ff 48 49 e2 84 78 70 10*ff 48 49 e2 84 78 71 10*ff 48 49 e2 84 78 72 10*ff
  //   48 49 e2 84 78 73 10*ff 68 70 14*ff 68 71 14*ff 68 72 14*ff 68 73 14*ff 48 49 e2 84 78 7 10*ff 48 49
  //   e2 84 78 17 10*ff 48 49 e2 84 78 27 10*ff 48 49 e2 84 78 37 10*ff 48 49 e2 84 75 8 57 9*ff 48 49 e2
  //   84 75 18 57 9*ff 48 49 e2 84 75 28 57 9*ff 48 49 e2 84 75 38 57 9*ff 48 49 e2 84 75 48 49 e2 84 78
  //   57 5*ff 48 49 e2 84 75 68 57 9*ff 68 75 48 49 e2 84 78 57 24*ff 68 7 14*ff 68 17 14*ff 68 27 14*ff
  //   68 37 14*ff 48 49 e2 84 9 7a e4 80 8*ff 48 49 e2 84 19 7a e4 81 8*ff 48 49 e2 84 29 7a e4 82 8*ff 48
  //   49 e2 84 39 7a e4 83 8*ff 48 49 e2 84 9 78 7a e4 80 7*ff 48 49 e2 84 19 78 7a e4 81 7*ff 48 49 e2 84
  //   29 78 7a e4 82 7*ff 48 49 e2 84 39 78 7a e4 83 7*ff 9 a e4 80 12*ff 9 1a e4 80 12*ff 9 2a e4 80
  //   12*ff 9 3a e4 80 12*ff 48 49 e2 84 9 7a e5 80 8*ff 48 49 e2 84 19 7a e5 81 8*ff 48 49 e2 84 29 7a e5
  //   82 8*ff 48 49 e2 84 39 7a e5 83 8*ff 48 49 e2 84 9 78 7a e5 80 7*ff 48 49 e2 84 19 78 7a e5 81 7*ff
  //   48 49 e2 84 29 78 7a e5 82 7*ff 48 49 e2 84 39 78 7a e5 83 7*ff 9 a e5 80 12*ff 9 1a e5 80 12*ff 9
  //   2a e5 80 12*ff 9 3a e5 80 12*ff 48 49 e2 84 9 7a e0 80 8*ff 48 49 e2 84 19 7a e0 81 8*ff 48 49 e2 84
  //   29 7a e0 82 8*ff 48 49 e2 84 39 7a e0 83 8*ff 48 49 e2 84 9 78 7a e0 80 7*ff 48 49 e2 84 19 78 7a e0
  //   81 7*ff 48 49 e2 84 29 78 7a e0 82 7*ff 48 49 e2 84 39 78 7a e0 83 7*ff 9 a e0 80 12*ff 9 1a e0 80
  //   12*ff 9 2a e0 80 12*ff 9 3a e0 80 12*ff 48 49 e2 84 9 7a e1 80 8*ff 48 49 e2 84 19 7a e1 81 8*ff 48
  //   49 e2 84 29 7a e1 82 8*ff 48 49 e2 84 39 7a e1 83 8*ff 48 49 e2 84 9 78 7a e1 80 7*ff 48 49 e2 84 19
  //   78 7a e1 81 7*ff 48 49 e2 84 29 78 7a e1 82 7*ff 48 49 e2 84 39 78 7a e1 83 7*ff 9 a e1 80 12*ff 9
  //   1a e1 80 12*ff 9 2a e1 80 12*ff 9 3a e1 80 12*ff a 48 49 e2 84 79 e1 80 8*ff 1a 48 49 e2 84 79 e1 81
  //   8*ff 2a 48 49 e2 84 79 e1 82 8*ff 3a 48 49 e2 84 79 e1 83 8*ff a 48 49 e2 84 78 79 e1 80 7*ff 1a 48
  //   49 e2 84 78 79 e1 81 7*ff 2a 48 49 e2 84 78 79 e1 82 7*ff 3a 48 49 e2 84 78 79 e1 83 7*ff a 9 e1 80
  //   12*ff a 19 e1 80 12*ff a 29 e1 80 12*ff a 39 e1 80 12*ff 9 eb 80 13*ff 19 eb 81 13*ff 29 eb 82 13*ff
  //   39 eb 83 13*ff a8 79 e2 89 aa e0 88 7 89 e2 88 17 89 e2 88 27 89 e2 88 37 89 aa e1 a8 87 7*ff a8 79
  //   aa e0 88 73 89 e3 88 72 89 e3 88 71 89 e3 88 70 89 e3 89 aa e1 a8 87 7*ff 9 e2 80 13*ff 19 e2 81
  //   13*ff 29 e2 82 13*ff 39 e2 83 13*ff 9 e3 80 13*ff 19 e3 81 13*ff 29 e3 82 13*ff 39 e3 83 13*ff 9 e6
  //   80 13*ff 19 e6 81 13*ff 29 e6 82 13*ff 39 e6 83 13*ff 9 e7 80 13*ff 19 e7 81 13*ff 29 e7 82 13*ff 39
  //   e7 83 13*ff 48 49 e2 84 9 7a e8 80 8*ff 48 49 e2 84 19 7a e8 81 8*ff 48 49 e2 84 29 7a e8 82 8*ff 48
  //   49 e2 84 39 7a e8 83 8*ff 48 49 e2 84 9 78 7a e8 80 7*ff 48 49 e2 84 19 78 7a e8 81 7*ff 48 49 e2 84
  //   29 78 7a e8 82 7*ff 48 49 e2 84 39 78 7a e8 83 7*ff 9 a e8 80 12*ff 9 1a e8 80 12*ff 9 2a e8 80
  //   12*ff 9 3a e8 80 12*ff 48 49 e2 84 9 7a e9 80 8*ff 48 49 e2 84 19 7a e9 81 8*ff 48 49 e2 84 29 7a e9
  //   82 8*ff 48 49 e2 84 39 7a e9 83 8*ff 48 49 e2 84 9 78 7a e9 80 7*ff 48 49 e2 84 19 78 7a e9 81 7*ff
  //   48 49 e2 84 29 78 7a e9 82 7*ff 48 49 e2 84 39 78 7a e9 83 7*ff 9 a e9 80 12*ff 9 1a e9 80 12*ff 9
  //   2a e9 80 12*ff 9 3a e9 80 12*ff 48 49 e2 84 9 7a ea 80 8*ff 48 49 e2 84 19 7a ea 81 8*ff 48 49 e2 84
  //   29 7a ea 82 8*ff 48 49 e2 84 39 7a ea 83 8*ff 48 49 e2 84 9 78 7a ea 80 7*ff 48 49 e2 84 19 78 7a ea
  //   81 7*ff 48 49 e2 84 29 78 7a ea 82 7*ff 48 49 e2 84 39 78 7a ea 83 7*ff 9 a ea 80 12*ff 9 1a ea 80
  //   12*ff 9 2a ea 80 12*ff 9 3a ea 80 12*ff 0 15*ff 10 15*ff 20 15*ff 30 15*ff 0 15*ff 1 15*ff 2 15*ff 3
  //   15*ff a8 79 e2 87 89 aa e0 88 7 7*ff a8 79 e2 87 89 aa e0 88 17 7*ff a8 79 e2 87 89 aa e0 88 27 7*ff
  //   a8 79 e2 87 89 aa e0 88 37 7*ff a8 79 e3 87 aa e0 88 70 8*ff a8 79 e3 87 aa e0 88 71 8*ff a8 79 e3
  //   87 aa e0 88 72 8*ff a8 79 e3 87 aa e0 88 73 40*ff 48 49 e2 84 78 79 f8 ec 8*ff 48 49 e2 84 78 79 f8
  //   ed 8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
  //   Toggle Extern RAM
endmodule

module Math (
  input  [15:0] A,
  input  [15:0] B,
  input  [3:0] Flags,
  output [15:0] Y,
  output Log_Cmp,
  output Log_Val
);

  wire adder_1_cout, and_1_out, and_3_out, and_4_out, and_5_out, and_6_out, and_7_out, and_8_out, and_9_out,
       and_10_out, and_11_out, decoder_1_out0, decoder_1_out1, decoder_1_out2, decoder_1_out3,
       multiplexer_3_out, not_1_out, not_4_out, not_5_out, not_6_out, not_7_out, not_8_out, not_9_out,
       not_10_out, not_11_out, or_1_out, or_3_out;
  wire [15:0] adder_1_out, and_2_out, multiplexer_1_out, multiplexer_2_out, not_2_out, not_3_out, or_2_out,
       shifter_1_out, shifter_2_out, xor_1_out;

  and and_1 (and_1_out, Flags[1], not_1_out);
  not not_1 (not_1_out, Flags[3]);
  Multiplexer #(.width(16)) multiplexer_1 (.in0(B), .in1(16'h1), .out(multiplexer_1_out), .sel(and_1_out));
  assign not_2_out = ~multiplexer_1_out;  // NOT_Gate not_2, 16 bits wide
  Multiplexer #(.width(16)) multiplexer_2 (
    .in0(multiplexer_1_out), .in1(not_2_out), .out(multiplexer_2_out), .sel(or_1_out));
  or or_1 (or_1_out, Flags[0], Flags[3]);
  assign not_3_out = ~A;  // NOT_Gate not_3, 16 bits wide
  assign xor_1_out = A ^ B;  // XOR_Gate xor_1, 16 bits wide
  assign or_2_out = A | B;  // OR_Gate or_2, 16 bits wide
  assign and_2_out = A & B;  // AND_Gate and_2, 16 bits wide
  Shifter #(.shift("lr"), .width(16)) shifter_1 (.in(A), .\dist (multiplexer_1_out[3:0]), .out(shifter_1_out));
  assign Y = and_3_out ? shifter_2_out : 16'bz;  // Controlled_Buffer controlled_buffer_1
  Shifter #(.width(16)) shifter_2 (.in(A), .\dist (multiplexer_1_out[3:0]), .out(shifter_2_out));
  and and_3 (and_3_out, Flags[2], not_4_out, not_5_out);
  assign Y = and_4_out ? adder_1_out : 16'bz;  // Controlled_Buffer controlled_buffer_2
  Adder #(.width(16)) adder_1 (.a(A), .b(multiplexer_2_out), .out(adder_1_out), .cin(or_1_out), .cout(adder_1_cout));
  and and_4 (and_4_out, not_6_out, not_7_out);
  not not_4 (not_4_out, Flags[3]);
  not not_5 (not_5_out, Flags[0]);
  not not_6 (not_6_out, Flags[2]);
  not not_7 (not_7_out, Flags[3]);
  or or_3 (or_3_out, xor_1_out[0], xor_1_out[1], xor_1_out[2], xor_1_out[3], xor_1_out[4], xor_1_out[5], xor_1_out[6], xor_1_out[7], xor_1_out[8], xor_1_out[9], xor_1_out[10], xor_1_out[11], xor_1_out[12], xor_1_out[13], xor_1_out[14], xor_1_out[15]);
  assign Y = and_5_out ? not_3_out : 16'bz;  // Controlled_Buffer controlled_buffer_3
  and and_5 (and_5_out, and_10_out, decoder_1_out3);
  assign Y = and_6_out ? xor_1_out : 16'bz;  // Controlled_Buffer controlled_buffer_4
  and and_6 (and_6_out, and_10_out, decoder_1_out2);
  assign Y = and_7_out ? or_2_out : 16'bz;  // Controlled_Buffer controlled_buffer_5
  and and_7 (and_7_out, and_10_out, decoder_1_out1);
  assign Y = and_8_out ? and_2_out : 16'bz;  // Controlled_Buffer controlled_buffer_6
  and and_8 (and_8_out, and_10_out, decoder_1_out0);
  assign Y = and_9_out ? shifter_1_out : 16'bz;  // Controlled_Buffer controlled_buffer_7
  and and_9 (and_9_out, Flags[2], not_4_out, not_8_out);
  and and_10 (and_10_out, Flags[3], not_11_out);
  not not_8 (not_8_out, not_5_out);
  not not_9 (not_9_out, adder_1_cout);
  and and_11 (and_11_out, adder_1_cout, or_3_out);
  not not_10 (not_10_out, or_3_out);
  Decoder #(.enable("false"), .select(2)) decoder_1 (
    .out0(decoder_1_out0), .out1(decoder_1_out1), .out2(decoder_1_out2), .out3(decoder_1_out3),
    .sel(Flags[1:0]));
  not not_11 (not_11_out, Flags[2]);
  and and_12 (Log_Cmp, Flags[2], Flags[3]);
  Multiplexer multiplexer_3 (.in0(not_10_out), .in1(or_3_out), .out(multiplexer_3_out), .sel(Flags[0]));
  Multiplexer #(.select(2)) multiplexer_4 (
    .in0(multiplexer_3_out), .in1(multiplexer_3_out), .in2(not_9_out), .in3(and_11_out), .out(Log_Val),
    .sel(Flags[1:0]));

  // Notes on the sheet:
  //   A >= B
endmodule

module DBG_out (
  input  [15:0] Data_in,
  input  DBG_in,
  input  DBGC_in,
  input  Clk,
  input  Reset,
  output [6:0] TTY_ASCII,
  output TTY_Clock,
  output TTY_Write
);

  wire and_1_out, and_2_out, d_ff_1_q, d_ff_2_q, d_ff_3_q, d_ff_4_q, Finish, or_2_out;
  wire [1:0] counter_1_q;
  wire [3:2] not_1_out;
  wire [6:0] multiplexer_1_out, value_to_hex_ascii_1_ascii_out;
  wire [15:0] DBG_q, shifter_1_out;

  Register #(.width(16)) DBG (.D(Data_in), .en(DBG_in), .clk(Clk), .Q(DBG_q), .clr(Reset));
  or or_1 (Finish, Reset, d_ff_4_q);
  D_Flip_Flop d_ff_1 (.D(or_2_out), .clk(Clk), .Q(d_ff_1_q), .reset(Finish));  // open: Qn, preset
  or or_2 (or_2_out, d_ff_1_q, DBG_in);
  Shifter #(.shift("lr"), .width(16)) shifter_1 (.in(DBG_q), .\dist ({not_1_out, 2'b00}), .out(shifter_1_out));
  and and_1 (and_1_out, Clk, d_ff_2_q);
  assign not_1_out = ~counter_1_q;  // NOT_Gate not_1, 2 bits wide
  and and_2 (and_2_out, counter_1_q[0], counter_1_q[1]);
  D_Flip_Flop d_ff_2 (.D(d_ff_1_q), .clk(Clk), .Q(d_ff_2_q), .reset(Finish));  // open: Qn, preset
  Counter #(.max('h3), .width(2)) counter_1 (
    .clr(Finish), .load(1'b0), .up(1'b1), .count(1'b1), .clk(and_1_out), .Q(counter_1_q));  // open: D, carry
  D_Flip_Flop d_ff_3 (.D(and_2_out), .clk(Clk), .Q(d_ff_3_q), .reset(Finish));  // open: Qn, preset
  D_Flip_Flop #(.trigger("falling")) d_ff_4 (
    .D(d_ff_3_q), .clk(Clk), .Q(d_ff_4_q), .reset(Finish));  // open: Qn, preset
  value_to_hex_ascii value_to_hex_ascii_1 (.data_in(shifter_1_out[3:0]), .ASCII_out(value_to_hex_ascii_1_ascii_out));
  Multiplexer #(.width(7)) multiplexer_1 (
    .in0(7'b0100000), .in1(value_to_hex_ascii_1_ascii_out), .out(multiplexer_1_out), .sel(d_ff_1_q));
  or or_3 (TTY_Write, d_ff_1_q, DBGC_in, DBG_in);
  Multiplexer #(.width(7)) multiplexer_2 (.in0(multiplexer_1_out), .in1(Data_in[6:0]), .out(TTY_ASCII), .sel(DBGC_in));

  assign TTY_Clock = Clk;
endmodule

module value_to_hex_ascii (
  input  [3:0] data_in,
  output [6:0] ASCII_out
);

  wire and_2_out, nand_1_out, or_1_out, or_2_out, xor_1_out;
  wire [2:0] not_1_out;

  or or_1 (or_1_out, data_in[0], data_in[1]);
  and and_1 (not_1_out[2], or_1_out, data_in[2]);
  nand nand_1 (nand_1_out, data_in[2], data_in[1]);
  Multiplexer multiplexer_1 (.in0(data_in[0]), .in1(xor_1_out), .out(not_1_out[1]), .sel(nand_1_out));
  xor xor_1 (xor_1_out, data_in[2], data_in[0]);
  not not_1 (not_1_out[0], data_in[0]);
  Multiplexer #(.width(7)) multiplexer_2 (
    .in0({3'b011, data_in}), .in1({4'b1100, not_1_out}), .out(ASCII_out), .sel(and_2_out));
  or or_2 (or_2_out, data_in[1], data_in[2]);
  and and_2 (and_2_out, or_2_out, data_in[3]);
endmodule
